// Digital circuit 4_Bit_Reg_v2.dig as structural Verilog
module _4_Bit_Reg_v2 (
  input  LD,
  input  D0,
  input  D1,
  input  D2,
  input  D3,
  input  CLK,
  input  EO,
  output O0,
  output O1,
  output O2,
  output O3
);

  wire and_1_out, and_2_out, and_3_out, and_4_out, and_5_out, and_6_out, and_7_out, and_8_out, and_9_out,
       d_latch_1_q, d_latch_2_q, d_latch_3_q, d_latch_4_q, not_1_out, not_2_out, not_3_out, not_4_out,
       or_1_out, or_2_out, or_3_out, or_4_out;

  and and_1 (and_1_out, EO, CLK);
  not not_1 (not_1_out, LD);
  not not_2 (not_2_out, LD);
  not not_3 (not_3_out, LD);
  not not_4 (not_4_out, LD);
  and and_2 (and_2_out, d_latch_1_q, not_1_out);
  and and_3 (and_3_out, LD, D0);
  and and_4 (and_4_out, d_latch_2_q, not_2_out);
  and and_5 (and_5_out, LD, D1);
  and and_6 (and_6_out, d_latch_3_q, not_3_out);
  and and_7 (and_7_out, LD, D2);
  and and_8 (and_8_out, d_latch_4_q, not_4_out);
  and and_9 (and_9_out, LD, D3);
  or or_1 (or_1_out, and_2_out, and_3_out);
  or or_2 (or_2_out, and_4_out, and_5_out);
  or or_3 (or_3_out, and_6_out, and_7_out);
  or or_4 (or_4_out, and_8_out, and_9_out);
  D_Latch d_latch_1 (.IN(or_1_out), .EN(CLK), .Q(d_latch_1_q));  // open: Q_2
  D_Latch d_latch_2 (.IN(or_2_out), .EN(CLK), .Q(d_latch_2_q));  // open: Q_2
  D_Latch d_latch_3 (.IN(or_3_out), .EN(CLK), .Q(d_latch_3_q));  // open: Q_2
  D_Latch d_latch_4 (.IN(or_4_out), .EN(CLK), .Q(d_latch_4_q));  // open: Q_2
  Tri_State_Buffer tri_state_buffer_1 (.IN(d_latch_1_q), .EN(and_1_out), .OUT(O0));
  Tri_State_Buffer tri_state_buffer_2 (.IN(d_latch_3_q), .EN(and_1_out), .OUT(O2));
  Tri_State_Buffer tri_state_buffer_3 (.IN(d_latch_2_q), .EN(and_1_out), .OUT(O1));
  Tri_State_Buffer tri_state_buffer_4 (.IN(d_latch_4_q), .EN(and_1_out), .OUT(O3));
endmodule
